# Fritzing sketch Strobe (saved by Fritzing 0.9.3b)

parts:
  R1 = Rotary Potentiometer (Large) [maximum_resistance=100kΩ package=THT]
  Part1 = Arduino Nano (Rev3.0)
  Q1 = MOSFET-NCHANNEL [package=to220v]
  JACK1 = 2.1mm Barrel Jack with Terminal Block
  R2 = Resistor [tolerance=±5% resistance=10k package=THT]

nets:
  N1: R1.leg1, Part1.AREF
  N2: R1.wiper, Part1.A0
  N3: R1.leg2, Part1.GND, Q1.S, JACK1.NEG, R2.Pin_1
  N4: Part1.D3, Q1.G, R2.Pin_0
  N5: Part1.VIN, JACK1.POS

notes:
  12V
  MOSFET
  Linear Potentiometer
  12V LED Panel
